// Logisim project Led_digital.circ as structural Verilog: 1 circuit, main circuit main
module main (
  input  in_1,
  input  in_2,
  input  in_3,
  input  in_4,
  input  in_5,
  input  in_6,
  input  in_7,
  input  in_8,
  input  in_9
);

  _7_Segment_Display u_7_segment_display_1 (
    .g(in_5), .f(in_4), .a(in_3), .b(in_2), .e(in_6), .d(in_7), .c(in_8), .dp(in_9));
endmodule
