// Logisim project complementar.circ as structural Verilog: 1 circuit, main circuit main
module main (
  input  in_1,
  input  in_2,
  input  in_3
);

  wire not_1_out, transistor_1_out, transistor_3_out;

  Transistor #(.\type ("n")) transistor_1 (.in(1'b1), .out(transistor_1_out), .gate(in_1));
  Transistor transistor_2 (.in(1'b0), .out(transistor_1_out), .gate(in_1));
  LED led_1 (.in(transistor_1_out));
  Transistor transistor_3 (.in(1'b1), .out(transistor_3_out), .gate(in_2));
  Transistor #(.\type ("n")) transistor_4 (.in(1'b0), .out(transistor_3_out), .gate(in_2));
  not not_1 (not_1_out, in_3);
  LED led_2 (.in(transistor_3_out));
  LED led_3 (.in(not_1_out));

  // Notes on the sheet:
  //   CHAVE Complementar
  //   porta logica NÃO
  //   NÃO complementar
endmodule
