// Logisim project e ou.circ as structural Verilog: 1 circuit, main circuit main
module main (
  input  C1,
  input  C1_2,
  input  C2,
  input  C2_2,
  input  C1_3,
  input  C1_4,
  input  C2_3,
  input  C2_4
);

  wire and_1_out, or_1_out, transistor_1_out, transistor_2_out, transistor_5_out, transistor_8_out;

  Transistor transistor_1 (.in(1'b0), .out(transistor_1_out), .gate(C1));
  Transistor #(.\type ("n")) transistor_2 (.in(1'b1), .out(transistor_2_out), .gate(C1));
  Transistor #(.\type ("n")) transistor_3 (.in(transistor_2_out), .out(transistor_1_out), .gate(C2_2));
  Transistor transistor_4 (.in(1'b0), .out(transistor_1_out), .gate(C2_2));
  and and_1 (and_1_out, C1_4, C2_4);
  LED led_1 (.in(transistor_1_out));
  LED led_2 (.in(and_1_out));
  Transistor #(.\type ("n")) transistor_5 (.in(1'b1), .out(transistor_5_out), .gate(C1_2));
  Transistor #(.\type ("n")) transistor_6 (.in(1'b1), .out(transistor_5_out), .gate(C2));
  Transistor transistor_7 (.in(transistor_8_out), .out(transistor_5_out), .gate(C1_2));
  Transistor transistor_8 (.in(1'b0), .out(transistor_8_out), .gate(C2));
  or or_1 (or_1_out, C1_3, C2_3);
  LED led_3 (.in(transistor_5_out));
  LED led_4 (.in(or_1_out));

  // Notes on the sheet:
  //   porta logica E
  //   E Complementar
  //   porta logica OU
  //   Ou Complementar
endmodule
