// Logisim project ferramentas.circ as structural Verilog: 1 circuit, main circuit main
module main (
  input  in_1,
  input  in_2,
  input  in_3,
  input  in_4
);

  wire pull_resistor_2_node, pull_resistor_3_node, transistor_1_out, transistor_4_out;

  Transistor #(.\type ("n")) transistor_1 (.in(1'b1), .out(transistor_1_out), .gate(in_1));
  Pull_Resistor pull_resistor_1 (.node(transistor_1_out));
  Pull_Resistor #(.pull(1)) pull_resistor_2 (.node(pull_resistor_2_node));
  Transistor #(.\type ("n")) transistor_2 (.in(1'b0), .out(pull_resistor_2_node), .gate(in_4));
  LED led_1 (.in(transistor_1_out));
  LED led_2 (.in(pull_resistor_2_node));
  Pull_Resistor #(.pull(1)) pull_resistor_3 (.node(pull_resistor_3_node));
  LED led_3 (.in(pull_resistor_3_node));
  Transistor transistor_3 (.in(1'b0), .out(pull_resistor_3_node), .gate(in_2));
  Transistor transistor_4 (.in(1'b1), .out(transistor_4_out), .gate(in_3));
  Pull_Resistor pull_resistor_4 (.node(transistor_4_out));
  LED led_4 (.in(transistor_4_out));

  // Notes on the sheet:
  //   -
  //   +
  //   +
  //   -
  //   CHAVE tipo N
  //   NÃO tipo N
  //   +
  //   -
  //   +
  //   -
  //   CHAVE tipo P
  //   NÃO tipo P
endmodule
